// Logisim project Chips.circ as structural Verilog: 6 circuits, main circuit XL74LS04
module XL74LS04 (
  input  [5:0] A,
  output [5:0] Y
);

  assign Y = ~A;  // NOT_Gate not_1, 6 bits wide
endmodule

module XL74LS08 (
  input  [3:0] A,
  input  [3:0] B,
  output [3:0] Y
);

  assign Y = A & B;  // AND_Gate and_1, 4 bits wide
endmodule

module XL74LS139 (
  input  [1:0] nG,
  input  [1:0] A,
  input  [1:0] B,
  output [1:0] Y0,
  output [1:0] Y1,
  output [1:0] Y2,
  output [1:0] Y3
);

  wire [1:0] not_1_out, not_2_out, not_3_out, not_4_out, not_5_out;

  assign not_1_out = ~nG;  // NOT_Gate not_1, 2 bits wide
  assign not_2_out = ~A;  // NOT_Gate not_2, 2 bits wide
  assign not_3_out = ~B;  // NOT_Gate not_3, 2 bits wide
  assign not_4_out = ~not_2_out;  // NOT_Gate not_4, 2 bits wide
  assign not_5_out = ~not_3_out;  // NOT_Gate not_5, 2 bits wide
  assign Y0 = ~(not_2_out & not_3_out & not_1_out);  // NAND_Gate nand_1, 2 bits wide
  assign Y1 = ~(not_1_out & not_3_out & not_4_out);  // NAND_Gate nand_2, 2 bits wide
  assign Y2 = ~(not_1_out & not_2_out & not_5_out);  // NAND_Gate nand_3, 2 bits wide
  assign Y3 = ~(not_1_out & not_4_out & not_5_out);  // NAND_Gate nand_4, 2 bits wide
endmodule

module SN74LS193DR (
  input  [3:0] D,
  input  MR,
  input  nPL,
  input  CPD,
  input  CPU,
  output nTCD,
  output [3:0] out_7,
  output nTCU
);

  wire and_1_out, and_2_out, and_3_out, and_4_out, comparator_1_eq, comparator_2_eq, not_1_out, or_1_out,
       or_2_out, or_3_out, xor_1_out;

  not not_1 (not_1_out, nPL);
  and and_1 (and_1_out, ~not_1_out, ~CPD, CPU);  // AND_Gate
  or or_1 (or_1_out, not_1_out, and_1_out);
  xor xor_1 (xor_1_out, CPU, CPD);
  and and_2 (and_2_out, ~not_1_out, xor_1_out);  // AND_Gate
  and and_3 (and_3_out, ~not_1_out, and_2_out);  // AND_Gate
  and and_4 (and_4_out, not_1_out, or_2_out);
  or or_2 (or_2_out, CPU, CPD);
  or or_3 (or_3_out, and_3_out, and_4_out);
  Counter #(.width(4), .max('hf)) counter_1 (
    .load(or_1_out), .D(D), .count(and_2_out), .Q(out_7), .clk(or_3_out), .clr(MR));  // open: carry
  Comparator #(.width(4)) comparator_1 (.a(4'b0000), .b(out_7), .eq(comparator_1_eq));  // open: gt, lt
  Comparator #(.width(4)) comparator_2 (.a(out_7), .b(4'b1111), .eq(comparator_2_eq));  // open: gt, lt
  nand nand_1 (nTCD, ~not_1_out, ~CPD, CPU, comparator_1_eq);  // NAND_Gate
  nand nand_2 (nTCU, comparator_2_eq, ~not_1_out, CPD, ~CPU);  // NAND_Gate
endmodule

module XL74LS00 (
  input  [3:0] A,
  input  [3:0] B,
  output [3:0] Y
);

  assign Y = ~(A & B);  // NAND_Gate nand_1, 4 bits wide
endmodule

module MC14490DWG (
  input  [3:0] In,
  input  OSC_In,
  output [3:0] Out,
  output OSC_OUT
);

  wire comparator_1_gt;

  assign Out = In & {4{OSC_In}};  // AND_Gate and_1, 4 bits wide
  Comparator #(.width(4)) comparator_1 (.a(In), .b(4'b0000), .gt(comparator_1_gt));  // open: eq, lt
  and and_2 (OSC_OUT, OSC_In, comparator_1_gt);
endmodule
