// Logisim project Computer.circ as structural Verilog: 5 circuits, main circuit main
module main (
  input  in_1
);

  wire bus_control_logic_1_npass_tru, CLK, CLK_HS, CLK_LS, HALT_LED, MODE0_LED, MODE1_LED, MODE2_LED,
       MODE_SW, nCLK, not_1_out, not_2_out, nPS_ON, Power_Switch, PULSE_SW, Reset_Switch, RST;
  wire [3:0] counter_1_q;
  wire [15:0] bus_control_logic_1_address_bus_2, bus_control_logic_1_data_bus_2, random_1_out, random_2_out;

  Button button_1 (.out(Power_Switch));
  Button button_2 (.out(Reset_Switch));
  Clock #(.highDuration(5), .lowDuration(5)) u_CLK_LS (.out(CLK_LS));
  Clock u_CLK_HS (.out(CLK_HS));
  Button button_3 (.out(PULSE_SW));
  Button button_4 (.out(MODE_SW));
  LED led_1 (.in(MODE0_LED));
  LED led_2 (.in(MODE1_LED));
  LED led_3 (.in(MODE2_LED));
  LED led_4 (.in(HALT_LED));
  LED led_5 (.in(CLK));
  LED led_6 (.in(nCLK));
  Counter #(.width(4), .max('hf)) counter_1 (.Q(counter_1_q), .clk(CLK));  // open: load, D, count, carry, clr
  Random #(.width(16)) random_1 (.clk(CLK), .out(random_1_out));  // open: next, clr
  Random #(.width(16)) random_2 (.clk(CLK), .out(random_2_out));  // open: next, clr
  Controlled_Buffer #(.width(16)) controlled_buffer_1 (
    .in(bus_control_logic_1_data_bus_2), .en(not_1_out));  // open: out
  Controlled_Buffer #(.width(16)) controlled_buffer_2 (
    .in(bus_control_logic_1_address_bus_2), .en(not_1_out));  // open: out
  // Probe on bus_control_logic_1_npass_tru
  Bus_Control_Logic bus_control_logic_1 (
    .Control({4'b0000, counter_1_q}), .CTRL_Address(8'h1), .nCLK(nCLK), .CLK(CLK), .RST(RST),
    .Data_BUS(random_1_out), .Address_BUS(random_2_out), .nPass_tru(bus_control_logic_1_npass_tru),
    .Data_BUS_2(bus_control_logic_1_data_bus_2), .Address_BUS_2(bus_control_logic_1_address_bus_2));
  // Probe on bus_control_logic_1_data_bus_2
  // Probe on bus_control_logic_1_address_bus_2
  not not_1 (not_1_out, bus_control_logic_1_npass_tru);
  not not_2 (not_2_out, nPS_ON);
  Power___PS_ON power_ps_on_1 (.SW(Power_Switch), .nPS_ON(nPS_ON));
  Clock_Control clock_control_1 (
    .CLK_LS(CLK_LS), .CLK_HS(CLK_HS), .Mode_sw(MODE_SW), .Pulse_sw(PULSE_SW), .RST(RST), .HLT(in_1),
    .CLK(CLK), .nCLK(nCLK), .nManual(MODE0_LED), .nAuto_LS(MODE1_LED), .nAuto_HS(MODE2_LED), .Halt(HALT_LED));
  Power___Reset power_reset_1 (.SW(Reset_Switch), .PWR_OK(not_2_out), .RST(RST));

  // Other names for the same wires on the sheet: HLT = in_1

  // Notes on the sheet:
  //   in_1: pull=down
endmodule

module Clock_Control (
  input  CLK_LS,
  input  CLK_HS,
  input  Mode_sw,
  input  Pulse_sw,
  input  RST,
  input  HLT,
  output CLK,
  output nCLK,
  output nManual,
  output nAuto_LS,
  output nAuto_HS,
  output Halt
);

  wire C0, C1, CLK_HLT, CLK_INT, CLK_NOT_HLT, MODE_RST, MODE_TRG, nCLK_HLT, nHLT, nMODE0, nMODE1, nMODE2,
       nMODE_RST, nRST, or_1_out, PULSE_TRG;
  wire [1:1] undriven, undriven_2, xl74ls139_1_y0, xl74ls139_1_y1, xl74ls139_1_y2, xl74ls139_1_y3;
  wire [2:0] xl74ls08_1_y;
  wire [3:2] mc14490dwg_1_out, sn74ls193dr_1_out_7;
  wire [3:3] undriven_3, undriven_4, xl74ls00_1_y;

  or or_1 (or_1_out, MODE_RST, RST);
  MC14490DWG mc14490dwg_1 (
    .In({2'b00, Mode_sw, Pulse_sw}), .OSC_In(1'b1), .Out({mc14490dwg_1_out, MODE_TRG, PULSE_TRG}));  // open: OSC_OUT
  SN74LS193DR sn74ls193dr_1 (
    .D(4'b1111), .MR(or_1_out), .nPL(nRST), .CPD(1'b1), .CPU(MODE_TRG), .out_7({sn74ls193dr_1_out_7, C1, C0}));  // open: nTCD, nTCU
  XL74LS04 xl74ls04_1 (
    .A({HLT, nMODE_RST, nMODE2, nMODE1, nMODE0, RST}), .Y({nHLT, MODE_RST, nAuto_HS, nAuto_LS, nManual, nRST}));
  XL74LS139 xl74ls139_1 (
    .nG(2'b00), .A({undriven[1], C0}), .B({undriven_2[1], C1}), .Y0({xl74ls139_1_y0[1], nMODE0}),
    .Y1({xl74ls139_1_y1[1], nMODE1}), .Y2({xl74ls139_1_y2[1], nMODE2}), .Y3({xl74ls139_1_y3[1], nMODE_RST}));
  or or_2 (CLK, CLK_HLT, CLK_NOT_HLT);
  XL74LS00 xl74ls00_1 (
    .A({undriven_3[3], CLK, nCLK_HLT, PULSE_TRG}), .B({undriven_4[3], CLK, nCLK_HLT, HLT}),
    .Y({xl74ls00_1_y[3], nCLK, CLK_HLT, nCLK_HLT}));
  XL74LS08 xl74ls08_1 (
    .A({nHLT, nAuto_HS, nAuto_LS, nManual}), .B({CLK_INT, CLK_HS, CLK_LS, PULSE_TRG}),
    .Y({CLK_NOT_HLT, xl74ls08_1_y}));
  or or_3 (CLK_INT, xl74ls08_1_y[0], xl74ls08_1_y[1], xl74ls08_1_y[2]);

  assign Halt = HLT;

  // Other names for the same wires on the sheet: MODE0 = nManual; MODE1 = nAuto_LS; MODE2 = nAuto_HS
endmodule

module Power___PS_ON (
  input  SW,
  output nPS_ON
);

  wire [1:0] n74hc74_653_1_q;
  wire [1:1] lp3470a293dbvr_1_rst_num, n74hc74_653_1_q_num;

  LP3470A293DBVR lp3470a293dbvr_1 (.RST_num(lp3470a293dbvr_1_rst_num[1]));
  _74HC74_653 u_74hc74_653_1 (
    .CP({1'b0, SW}), .D(2'b01), .SD_num(2'b11), .RD_num({2{lp3470a293dbvr_1_rst_num[1]}}),
    .Q(n74hc74_653_1_q), .Q_num({n74hc74_653_1_q_num[1], nPS_ON}));
endmodule

module Power___Reset (
  input  SW,
  input  PWR_OK,
  output RST
);

  wire [0:0] lp3470a293dbvr_1_rst_num;
  wire [5:0] xl74ls04_1_y;

  LP3470A293DBVR lp3470a293dbvr_1 (.RST_num(lp3470a293dbvr_1_rst_num[0]));
  XL74LS04 xl74ls04_1 (.A({4'b0000, PWR_OK, lp3470a293dbvr_1_rst_num[0]}), .Y(xl74ls04_1_y));
  or or_1 (RST, SW, xl74ls04_1_y[0], xl74ls04_1_y[1]);
endmodule

module Bus_Control_Logic (
  input  [7:0] Control,
  input  [7:0] CTRL_Address,
  input  nCLK,
  input  CLK,
  input  RST,
  input  [15:0] Data_BUS,
  input  [15:0] Address_BUS,
  output nPass_tru,
  output [15:0] Data_BUS_2,
  output [15:0] Address_BUS_2
);

  wire CTRL_ACTIVE, CTRL_LATCH, CTRL_RESET, n74hct85d_653_1_out_6, n74hct85d_653_1_out_7,
       n74hct85d_653_1_out_8, n74hct85d_653_2_out_6, n74hct85d_653_2_out_7, n74hct85d_653_2_out_8,
       nCTRL_LATCH, nCTRL_RESET;
  wire [1:0] n74hc74_653_1_q_num;
  wire [1:1] n74hc74_653_1_q, undriven_3, undriven_4, undriven_5, undriven_7;
  wire [3:0] xl74ls08_1_y_2, xl74ls08_2_y;
  wire [3:2] undriven;
  wire [3:3] undriven_2, xl74ls08_1_y;
  wire [5:3] undriven_6, xl74ls04_1_y;
  wire [7:0] gr_74hc574ts_1_q;

  _74HCT85D_653 u_74hct85d_653_1 (
    .IN(1'b0), .IN_2(1'b1), .IN_3(1'b0), .A(Control[3:0]), .B(CTRL_Address[3:0]),
    .out_8(n74hct85d_653_1_out_8), .out_7(n74hct85d_653_1_out_7), .out_6(n74hct85d_653_1_out_6));
  _74HCT85D_653 u_74hct85d_653_2 (
    .IN(1'b0), .IN_2(1'b1), .IN_3(1'b0), .A(Control[3:0]), .B(4'b1111), .out_8(n74hct85d_653_2_out_8),
    .out_7(n74hct85d_653_2_out_7), .out_6(n74hct85d_653_2_out_6));
  _74HC74_653 u_74hc74_653_1 (
    .CP({undriven_3[1], CLK}), .D({undriven_4[1], CTRL_ACTIVE}), .SD_num({undriven_7[1], nCTRL_LATCH}),
    .RD_num({undriven_5[1], nCTRL_RESET}), .Q({n74hc74_653_1_q[1], CTRL_LATCH}), .Q_num(n74hc74_653_1_q_num));
  XL74LS04 xl74ls04_1 (
    .A({undriven_6, RST, CTRL_LATCH, CTRL_RESET}), .Y({xl74ls04_1_y, undriven[2], nCTRL_LATCH, nCTRL_RESET}));
  XL74LS08 xl74ls08_1 (
    .A({undriven, {2{CLK}}}), .B({undriven_2[3], nCTRL_RESET, CTRL_RESET, CTRL_ACTIVE}),
    .Y({xl74ls08_1_y_2[3], xl74ls08_1_y[3], xl74ls08_1_y_2[1:0]}));
  GR_74HC574TS gr_74hc574ts_1 (.OE_num(1'b0), .CLK(nPass_tru), .D({4'b0000, xl74ls08_2_y}), .Q(gr_74hc574ts_1_q));
  XL74LS08 xl74ls08_2 (.A({4{xl74ls08_1_y[3]}}), .B(Data_BUS[3:0]), .Y(xl74ls08_2_y));
  _74HCT85D_653 u_74hct85d_653_3 (
    .IN(n74hct85d_653_1_out_8), .IN_2(n74hct85d_653_1_out_7), .IN_3(n74hct85d_653_1_out_6), .A(Control[7:4]),
    .B(CTRL_Address[7:4]), .out_7(CTRL_ACTIVE));  // open: out_8, out_6
  _74HCT85D_653 u_CTRL_RESET (
    .IN(n74hct85d_653_2_out_8), .IN_2(n74hct85d_653_2_out_7), .IN_3(n74hct85d_653_2_out_6), .A(Control[7:4]),
    .B(4'b1111), .out_7(CTRL_RESET));  // open: out_8, out_6
  or or_1 (nPass_tru, xl74ls08_1_y_2[0], xl74ls08_1_y_2[1]);
  // Probe on gr_74hc574ts_1_q
  SN74LS541DWR sn74ls541dwr_1 (.G1_num(nPass_tru), .G2_num(1'b0), .A(Data_BUS[7:0]), .out_4(Data_BUS_2[7:0]));
  SN74LS541DWR sn74ls541dwr_2 (.G1_num(nPass_tru), .G2_num(1'b0), .A(Data_BUS[15:8]), .out_4(Data_BUS_2[15:8]));
  SN74LS541DWR sn74ls541dwr_3 (.G1_num(nPass_tru), .G2_num(1'b0), .A(Address_BUS[7:0]), .out_4(Address_BUS_2[7:0]));
  SN74LS541DWR sn74ls541dwr_4 (.G1_num(nPass_tru), .G2_num(1'b0), .A(Address_BUS[15:8]), .out_4(Address_BUS_2[15:8]));
  Pull_Resistor pull_resistor_1 (.node(Data_BUS_2));
  Pull_Resistor pull_resistor_2 (.node(Address_BUS_2));

  // Notes on the sheet:
  //   0xFF = CTRL RESET, Reset all controls
endmodule
